// Logisim project wikiarduino.circ as structural Verilog: 1 circuit, main circuit main
module main (
  input  _9,
  input  _8,
  input  _7,
  input  _6,
  input  _5,
  input  _4,
  input  _3,
  input  _2,
  input  in_9,
  input  in_10,
  input  in_11,
  input  in_12,
  input  in_13,
  input  in_14,
  output a0,
  output a1,
  output a2,
  output a3,
  output a4,
  output a5
);

  LED led_1 (.in(_8));
  LED led_2 (.in(_7));
  LED led_3 (.in(_9));
  LED led_4 (.in(_6));
  LED led_5 (.in(_2));
  LED led_6 (.in(_5));
  LED led_7 (.in(_3));
  LED led_8 (.in(_4));

  assign a0 = in_9;
  assign a1 = in_10;
  assign a2 = in_11;
  assign a3 = in_12;
  assign a4 = in_13;
  assign a5 = in_14;

  // Notes on the sheet:
  //   il numero sotto il pin è il numero del pin sulla board di arduino
  //   collegamento con i sensori ... il pin a0 gestisce unicamente il sensore di temperatura
  //   quindi contiene al suo interno già la conversione in temperatura
  //   gli altri pin invece restituiscono semplicemente il valore grezzo
endmodule
